// Logisim project Calculator.circ as structural Verilog
module FullAdder (
  input  A,
  input  B,
  input  Cin,
  output Sum,
  output Cout
);

  wire and_1_out, and_2_out, xor_1_out;

  xor xor_1 (xor_1_out, A, B);
  xor xor_2 (Sum, xor_1_out, Cin);
  and and_1 (and_1_out, xor_1_out, Cin);
  and and_2 (and_2_out, A, B);
  or or_1 (Cout, and_1_out, and_2_out);
endmodule

module Adder8bit (
  input  in_1,
  input  in_2,
  input  in_3,
  input  in_4,
  input  in_5,
  input  in_6,
  input  in_7,
  input  in_8,
  input  in_9,
  input  in_10,
  input  in_11,
  input  in_12,
  input  in_13,
  input  in_14,
  input  in_15,
  input  in_16,
  output S0,
  output S1,
  output S2,
  output S3,
  output S4,
  output S5,
  output S6,
  output S7,
  output Cout
);

  wire FA0_cout, FA1_cout, FA2_cout, FA3_cout, FA4_cout, FA5_cout, FA6_cout;

  FullAdder FA0 (.A(in_2), .B(in_1), .Cin(1'b0), .Sum(S0), .Cout(FA0_cout));
  FullAdder FA1 (.A(in_4), .B(in_3), .Cin(FA0_cout), .Sum(S1), .Cout(FA1_cout));
  FullAdder FA2 (.A(in_6), .B(in_5), .Cin(FA1_cout), .Sum(S2), .Cout(FA2_cout));
  FullAdder FA3 (.A(in_8), .B(in_7), .Cin(FA2_cout), .Sum(S3), .Cout(FA3_cout));
  FullAdder FA4 (.A(in_10), .B(in_9), .Cin(FA3_cout), .Sum(S4), .Cout(FA4_cout));
  FullAdder FA5 (.A(in_12), .B(in_11), .Cin(FA4_cout), .Sum(S5), .Cout(FA5_cout));
  FullAdder FA6 (.A(in_14), .B(in_13), .Cin(FA5_cout), .Sum(S6), .Cout(FA6_cout));
  FullAdder FA7 (.A(in_16), .B(in_15), .Cin(FA6_cout), .Sum(S7), .Cout(Cout));
endmodule
